# Fritzing sketch 4049 (saved by Fritzing 0.9.2b)
breadboards: 1

parts:
  IC1 = IC, DIP package, 16 pins [chip_label=4049]
  LED1 = LED - 5mm [color="Red (633nm)" package="5 mm [THT]"]
  R1 = Resistor [tolerance=±5% resistance=330 package=THT]
  VCC1 = Battery
  S1 = Pushbutton [package="[THT]"]

nets:
  N1: IC1.pin1, VCC1.+, S1.Pin_3, S1.Pin_4
  N2: IC1.pin2, R1.Pin_1
  N3: IC1.pin3, S1.Pin_1, S1.Pin_2
  N4: IC1.pin8, LED1.cathode, VCC1.-
  N5: LED1.anode, R1.Pin_0
