# Fritzing sketch 4077 (saved by Fritzing 0.9.2b)
breadboards: 1

parts:
  VCC1 = Battery
  S1 = Pushbutton [package="[THT]"]
  S2 = Pushbutton [package="[THT]"]
  LED1 = LED - 5mm [color="Red (633nm)" package="5 mm [THT]"]
  R1 = Resistor [tolerance=±5% resistance=330 package=THT]
  IC1 = IC, DIP package, 14 pins [chip_label=4077]

nets:
  N1: VCC1.-, LED1.cathode, IC1.pin7
  N2: VCC1.+, S1.Pin_3, S1.Pin_4, S2.Pin_3, S2.Pin_4, IC1.pin14
  N3: S1.Pin_1, S1.Pin_2, IC1.pin2
  N4: S2.Pin_1, S2.Pin_2, IC1.pin1
  N5: LED1.anode, R1.Pin_0
  N6: R1.Pin_1, IC1.pin3
